# Fritzing sketch Pressto_Fritzing (saved by Fritzing 0.9.2b)
breadboards: 1

parts:
  Part1 = Arduino Uno (Rev3)
  Part2 = EasyDriver_v44
  Power_plug1 = Power plug
  Power_plug2 = Power plug
  S1 = Pushbutton [package="[THT]"]
  S2 = Pushbutton [package="[THT]"]
  R1 = Resistor [tolerance=±5% resistance=220 package=THT]
  R2 = Resistor [tolerance=±5% resistance=220 package=THT]

nets:
  GND: Part1.D12/MISO, Part1.D13/SCK, Part1.GND, Part2.ENABLE, Power_plug1.GND, S1.Pin_1, S1.Pin_2, S1.Pin_3, S1.Pin_4, S2.Pin_1, S2.Pin_2, S2.Pin_3, S2.Pin_4, R1.Pin_0, R2.Pin_0
  N1: Part1.D0/RX, Part2.MS1
  N2: Part1.D1/TX, Part2.MS2
  N3: Part1.D2, Part2.DIR
  N4: Part1.D3_PWM, Part2.STEP
  VIN: Part1.VIN, Power_plug1.VCC, R1.Pin_1, R2.Pin_1
  GND_2: Part2.GND, Power_plug2.GND
  N5: Part2.V+, Power_plug2.VCC
